# Fritzing sketch Pokemon (saved by Fritzing 0.9.3b)
breadboards: 2

parts:
  Raspberry_Pi_1 = Raspberry Pi 3 [part_number=RPI-3-V1.2]
  LED1 = LED - 5mm [color="Red (633nm)" package="5 mm [THT]"]
  LED2 = LED - 5mm [color="Red (633nm)" package="5 mm [THT]"]
  LED3 = LED - 5mm [color="Red (633nm)" package="5 mm [THT]"]
  R1 = Resistor [tolerance=±5% resistance=220 package=THT]
  R2 = Resistor [tolerance=±5% resistance=220 package=THT]
  R3 = Resistor [tolerance=±5% resistance=220 package=THT]
  R4 = Rotary Potentiometer (Small) [maximum_resistance=100kΩ package=THT]
  J1 = Basic Force Sensing Resistor (FSR) [package=THT]
  R5 = Resistor [tolerance=±5% resistance=220 package="2010 [SMD]"]
  IC1 = PICAXE-08 [package=THT]
  IC2 = PICAXE-08 [package=THT]

nets:
  N1: Raspberry_Pi_1.3v3, J1.pin_0, IC1.Serial_Out_/_Out_0, IC1.0V
  N2: Raspberry_Pi_1.GPIO2, LED3.cathode
  N3: Raspberry_Pi_1.GPIO3, LED2.cathode
  N4: Raspberry_Pi_1.GIPO4, LED1.cathode
  N5: Raspberry_Pi_1.GND, R1.Pin_0, R2.Pin_0, R3.Pin_0, R4.leg2, R5.Pin_0, IC1.In/Out_1, IC2.In/Out_2
  N6: Raspberry_Pi_1.GIPO19, R4.wiper
  N7: Raspberry_Pi_1.GIPO25, IC2.In/Out_1
  N8: Raspberry_Pi_1.GIPO24, IC2.Serial_Out_/_Out_0
  N9: Raspberry_Pi_1.GIPO23, IC2.0V
  N10: Raspberry_Pi_1.GIPO18, IC1.In/Out_2
  N11: Raspberry_Pi_1.5V, R4.leg1
  N12: LED1.anode, R1.Pin_1
  N13: LED2.anode, R2.Pin_1
  N14: LED3.anode, R3.Pin_1
  N15: J1.pin_1, R5.Pin_1, IC1.+V
